// Logisim project program13.circ as structural Verilog
module d_a_b_c (
  input  a,
  input  b,
  input  c,
  output d0,
  output d1,
  output d2,
  output d3,
  output d4,
  output d5,
  output d6,
  output d7
);

  wire and_1_out, and_2_out, and_3_out, and_5_out, and_7_out, and_9_out, and_11_out, and_13_out, not_1_out,
       not_2_out, not_3_out, not_4_out, not_5_out, not_6_out, not_7_out, not_8_out, not_9_out, not_10_out,
       not_11_out, not_12_out;

  not not_1 (not_1_out, a);
  not not_2 (not_2_out, b);
  not not_3 (not_3_out, a);
  not not_4 (not_4_out, b);
  not not_5 (not_5_out, a);
  not not_6 (not_6_out, a);
  not not_7 (not_7_out, b);
  not not_8 (not_8_out, b);
  and and_1 (and_1_out, a, b);
  not not_9 (not_9_out, c);
  and and_2 (and_2_out, a, b);
  and and_3 (and_3_out, not_1_out, not_2_out);
  and and_4 (d0, and_3_out, not_10_out);
  not not_10 (not_10_out, c);
  and and_5 (and_5_out, not_3_out, not_4_out);
  and and_6 (d1, and_5_out, c);
  and and_7 (and_7_out, not_5_out, b);
  and and_8 (d2, and_7_out, not_11_out);
  not not_11 (not_11_out, c);
  and and_9 (and_9_out, not_6_out, b);
  and and_10 (d3, and_9_out, c);
  and and_11 (and_11_out, a, not_7_out);
  and and_12 (d4, and_11_out, not_12_out);
  not not_12 (not_12_out, c);
  and and_13 (and_13_out, a, not_8_out);
  and and_14 (d5, and_13_out, c);
  and and_15 (d6, and_1_out, not_9_out);
  and and_16 (d7, and_2_out, c);
endmodule
