// Logisim project program14.circ as structural Verilog: 1 circuit, main circuit main
module main (
  input  [3:0] in_1,
  input  [3:0] in_2,
  output out_3,
  output out_4,
  output out_5
);

  Comparator #(.width(4)) comparator_1 (.a(in_1), .b(in_2), .gt(out_3), .eq(out_4), .lt(out_5));

  // Notes on the sheet:
  //   A
  //   B
endmodule
