// Logisim project program16.circ as structural Verilog: 1 circuit, main circuit main
module main (
  input  in_1,
  input  in_2,
  input  in_3,
  input  in_4,
  input  in_5,
  input  in_6,
  input  in_7,
  input  in_8,
  input  in_9,
  input  in_10,
  input  in_11,
  output out_12,
  output out_13,
  output out_14
);

  wire and_1_out, and_2_out, and_3_out, and_4_out, and_5_out, and_6_out, button_1_out, button_2_out,
       button_3_out, button_4_out, clock_1_out, clock_2_out, clock_3_out, clock_4_out, d_ff_1_q, d_ff_2_q,
       d_ff_3_q, d_ff_5_q, d_ff_6_q, d_ff_7_q, d_ff_8_q, d_ff_9_q, d_ff_10_q, d_ff_13_q, d_ff_16_q,
       not_1_out, or_1_out, or_2_out, or_3_out, undriven, undriven_2, undriven_3, undriven_4, undriven_5;

  Clock clock_1 (.out(clock_1_out));
  Button button_1 (.out(button_1_out));
  Clock clock_2 (.out(clock_2_out));
  Button button_2 (.out(button_2_out));
  Clock clock_3 (.out(clock_3_out));
  Button button_3 (.out(button_3_out));
  Clock clock_4 (.out(clock_4_out));
  Button button_4 (.out(button_4_out));
  D_Flip_Flop d_ff_1 (.clk(clock_1_out), .D(in_1), .Q(d_ff_1_q), .reset(button_1_out));  // open: Qn, preset, en
  D_Flip_Flop d_ff_2 (.clk(clock_3_out), .D(in_3), .Q(d_ff_2_q), .reset(button_3_out));  // open: Qn, preset, en
  LED led_1 ();  // open: in
  not not_1 (not_1_out, in_11);
  LED led_2 (.in(d_ff_3_q));
  D_Flip_Flop d_ff_3 (.clk(clock_2_out), .D(in_2), .Q(d_ff_3_q), .reset(button_2_out));  // open: Qn, preset, en
  D_Flip_Flop d_ff_4 (.clk(clock_4_out), .D(not_1_out));  // open: Q, Qn, preset, en, reset
  D_Flip_Flop d_ff_5 (.clk(clock_1_out), .D(d_ff_1_q), .Q(d_ff_5_q), .reset(button_1_out));  // open: Qn, preset, en
  LED led_3 (.in(d_ff_6_q));
  D_Flip_Flop d_ff_6 (.clk(clock_2_out), .D(d_ff_3_q), .Q(d_ff_6_q), .reset(button_2_out));  // open: Qn, preset, en
  D_Flip_Flop d_ff_7 (.clk(clock_3_out), .D(in_4), .Q(d_ff_7_q), .reset(button_3_out));  // open: Qn, preset, en
  LED led_4 ();  // open: in
  and and_1 (and_1_out, undriven, in_11);
  or or_1 (or_1_out, and_1_out, and_2_out);
  D_Flip_Flop d_ff_8 (.clk(clock_1_out), .D(d_ff_5_q), .Q(d_ff_8_q), .reset(button_1_out));  // open: Qn, preset, en
  LED led_5 (.in(d_ff_9_q));
  D_Flip_Flop d_ff_9 (.clk(clock_2_out), .D(d_ff_6_q), .Q(d_ff_9_q), .reset(button_2_out));  // open: Qn, preset, en
  D_Flip_Flop d_ff_10 (.clk(clock_3_out), .D(in_5), .Q(d_ff_10_q), .reset(button_3_out));  // open: Qn, preset, en
  LED led_6 ();  // open: in
  and and_2 (and_2_out, not_1_out, undriven_2);
  D_Flip_Flop d_ff_11 (.clk(clock_2_out), .D(d_ff_9_q), .Q(out_13), .reset(button_2_out));  // open: Qn, preset, en
  D_Flip_Flop d_ff_12 (.clk(clock_3_out), .D(in_6), .Q(out_14), .reset(button_3_out));  // open: Qn, preset, en
  and and_3 (and_3_out, d_ff_13_q, in_11);
  D_Flip_Flop d_ff_13 (.clk(clock_4_out), .D(or_1_out), .Q(d_ff_13_q), .reset(button_4_out));  // open: Qn, preset, en
  D_Flip_Flop d_ff_14 (.clk(clock_1_out), .D(d_ff_8_q), .Qn(out_12), .reset(button_1_out));  // open: Q, preset, en
  LED led_7 (.in(out_13));
  LED led_8 ();  // open: in
  or or_2 (or_2_out, and_3_out, and_4_out);
  and and_4 (and_4_out, not_1_out, undriven_3);
  D_Flip_Flop d_ff_15 (.clk(clock_4_out), .D(or_2_out), .reset(button_4_out));  // open: Q, Qn, preset, en
  and and_5 (and_5_out, undriven_4, in_11);
  or or_3 (or_3_out, and_5_out, and_6_out);
  and and_6 (and_6_out, not_1_out, undriven_5);
  D_Flip_Flop d_ff_16 (.clk(clock_4_out), .D(or_3_out), .Q(d_ff_16_q), .reset(button_4_out));  // open: Qn, preset, en
  LED led_9 (.in(d_ff_16_q));
endmodule
