// Logisim project program5.circ as structural Verilog
module f_a_b_c (
  input  a,
  input  b,
  input  c,
  output f
);

  wire and_1_out, not_1_out;

  not not_1 (not_1_out, a);
  and and_1 (and_1_out, not_1_out, b);
  or or_1 (f, c, and_1_out);
endmodule

module f_a_b_c_2 (
  input  a,
  input  b,
  input  c,
  output f
);

  wire and_1_out, not_1_out;

  not not_1 (not_1_out, a);
  and and_1 (and_1_out, not_1_out, b);
  or or_1 (f, c, and_1_out);
endmodule
