// Logisim project program6.circ as structural Verilog
module f_a_b_c_d (
  input  a,
  input  b,
  input  c,
  input  d,
  output f
);

  wire and_1_out, and_2_out, not_1_out, not_2_out;

  not not_1 (not_1_out, b);
  not not_2 (not_2_out, d);
  and and_1 (and_1_out, not_1_out, not_2_out);
  and and_2 (and_2_out, b, d);
  or or_1 (f, and_1_out, and_2_out);
endmodule

module f_a_b_c_d_2 (
  input  a,
  input  b,
  input  c,
  input  d,
  output f
);

  wire and_1_out, and_2_out, not_1_out, not_2_out;

  not not_1 (not_1_out, b);
  not not_2 (not_2_out, d);
  and and_1 (and_1_out, not_1_out, not_2_out);
  and and_2 (and_2_out, b, d);
  or or_1 (f, and_1_out, and_2_out);
endmodule
